// Logisim project ALU Finished.circ as structural Verilog: 4 circuits, main circuit main
module main (
  input  [7:0] A,
  input  [7:0] B,
  input  [5:0] FUNCT,
  output [7:0] Output
);

  wire alu_controller_1_anegate, alu_controller_1_bnegate;
  wire [1:0] alu_controller_1_op;

  ALU_controller alu_controller_1 (
    .FUNCT(FUNCT), .ANegate(alu_controller_1_anegate), .Bnegate(alu_controller_1_bnegate),
    .OP(alu_controller_1_op));
  _8BitALU u_8bitalu_1 (
    .A(A), .B(B), .Output(Output), .Anegate(alu_controller_1_anegate), .Bnegate(alu_controller_1_bnegate),
    .Operation(alu_controller_1_op));

  // Notes on the sheet:
  //   ALU Controller
  //   ALU
endmodule

module _8BitALU (
  input  Anegate,
  input  Bnegate,
  input  [1:0] Operation,
  input  [7:0] A,
  input  [7:0] B,
  output [7:0] Output
);

  wire n1bitalu_1_carryout, n1bitalu_2_carryout, n1bitalu_3_carryout, n1bitalu_4_carryout,
       n1bitalu_5_carryout, n1bitalu_6_carryout, n1bitalu_7_carryout;

  _1BitALU u_1bitalu_1 (
    .A(A[0]), .B(B[0]), .Result(Output[0]), .AInvert(Anegate), .BInvert(Bnegate), .CarryIn(Bnegate),
    .Selector(Operation), .CarryOut(n1bitalu_1_carryout));
  _1BitALU u_1bitalu_2 (
    .A(A[1]), .B(B[1]), .Result(Output[1]), .AInvert(Anegate), .BInvert(Bnegate),
    .CarryIn(n1bitalu_1_carryout), .Selector(Operation), .CarryOut(n1bitalu_2_carryout));
  _1BitALU u_1bitalu_3 (
    .A(A[2]), .B(B[2]), .Result(Output[2]), .AInvert(Anegate), .BInvert(Bnegate),
    .CarryIn(n1bitalu_2_carryout), .Selector(Operation), .CarryOut(n1bitalu_3_carryout));
  _1BitALU u_1bitalu_4 (
    .A(A[3]), .B(B[3]), .Result(Output[3]), .AInvert(Anegate), .BInvert(Bnegate),
    .CarryIn(n1bitalu_3_carryout), .Selector(Operation), .CarryOut(n1bitalu_4_carryout));
  _1BitALU u_1bitalu_5 (
    .A(A[4]), .B(B[4]), .Result(Output[4]), .AInvert(Anegate), .BInvert(Bnegate),
    .CarryIn(n1bitalu_4_carryout), .Selector(Operation), .CarryOut(n1bitalu_5_carryout));
  _1BitALU u_1bitalu_6 (
    .A(A[5]), .B(B[5]), .Result(Output[5]), .AInvert(Anegate), .BInvert(Bnegate),
    .CarryIn(n1bitalu_5_carryout), .Selector(Operation), .CarryOut(n1bitalu_6_carryout));
  _1BitALU u_1bitalu_7 (
    .A(A[6]), .B(B[6]), .Result(Output[6]), .AInvert(Anegate), .BInvert(Bnegate),
    .CarryIn(n1bitalu_6_carryout), .Selector(Operation), .CarryOut(n1bitalu_7_carryout));
  _1BitALU u_1bitalu_8 (
    .A(A[7]), .B(B[7]), .Result(Output[7]), .AInvert(Anegate), .BInvert(Bnegate),
    .CarryIn(n1bitalu_7_carryout), .Selector(Operation));  // open: CarryOut
endmodule

module ALU_controller (
  input  [5:0] FUNCT,
  output ANegate,
  output Bnegate,
  output [1:0] OP
);

  wire and_2_out;
  wire [2:0] multiplexer_2_out;

  and and_1 (ANegate, FUNCT[0], FUNCT[1], FUNCT[2]);
  and and_2 (and_2_out, FUNCT[5], FUNCT[5]);
  Multiplexer #(.select(3), .width(2), .enable("false")) multiplexer_1 (
    .in0(2'b10), .in2(2'b10), .in4(2'b00), .in5(2'b01), .in7(2'b00), .out(OP), .sel(multiplexer_2_out));  // open: in1, in3, in6
  Multiplexer #(.width(3), .enable("false")) multiplexer_2 (
    .in1(FUNCT[2:0]), .out(multiplexer_2_out), .sel(and_2_out));  // open: in0

  assign Bnegate = FUNCT[1];

  // Notes on the sheet:
  //   add: 32: 0010, sub: 34: 0110, and: 36: 0000, or: 37: 0001 nor: 39: 1100
endmodule

module _1BitALU (
  input  AInvert,
  input  BInvert,
  input  CarryIn,
  input  [1:0] Selector,
  input  A,
  input  B,
  output Result,
  output CarryOut
);

  wire adder_1_out, and_1_out, multiplexer_1_out, multiplexer_2_out, not_1_out, not_2_out, or_1_out;

  not not_1 (not_1_out, A);
  Multiplexer #(.enable("false")) multiplexer_1 (.in0(A), .in1(not_1_out), .out(multiplexer_1_out), .sel(AInvert));
  Multiplexer #(.enable("false")) multiplexer_2 (.in0(B), .in1(not_2_out), .out(multiplexer_2_out), .sel(BInvert));
  not not_2 (not_2_out, B);
  Adder #(.width(1)) adder_1 (
    .a(multiplexer_1_out), .b(multiplexer_2_out), .out(adder_1_out), .cin(CarryIn), .cout(CarryOut));
  and and_1 (and_1_out, multiplexer_1_out, multiplexer_2_out);
  or or_1 (or_1_out, multiplexer_1_out, multiplexer_2_out);
  Multiplexer #(.select(2), .enable("false")) multiplexer_3 (
    .in0(and_1_out), .in1(or_1_out), .in2(adder_1_out), .out(Result), .sel(Selector));  // open: in3
endmodule
