// Logisim project Logism.circ as structural Verilog
module _2_Bit_Decoder (
  input  A,
  input  B,
  output _00,
  output _01,
  output _10,
  output _11
);

  wire not_1_out, not_2_out, not_3_out, not_4_out;

  not not_1 (not_1_out, A);
  not not_2 (not_2_out, B);
  not not_3 (not_3_out, A);
  not not_4 (not_4_out, B);
  and and_1 (_00, not_1_out, not_2_out);
  and and_2 (_01, not_3_out, B);
  and and_3 (_10, A, not_4_out);
  and and_4 (_11, A, B);
endmodule

module _1_Bit_4_Input_Multiplexer (
  input  A___00,
  input  B___01,
  input  C___10,
  input  D___11,
  input  in_5,
  input  in_6,
  output Selected_Output
);

  wire and_1_out, and_2_out, and_3_out, and_4_out, n2_bit_decoder_1__00, n2_bit_decoder_1__01,
       n2_bit_decoder_1__10, n2_bit_decoder_1__11;

  _2_Bit_Decoder u_2_bit_decoder_1 (
    .A(in_5), .B(in_6), ._00(n2_bit_decoder_1__00), ._01(n2_bit_decoder_1__01), ._10(n2_bit_decoder_1__10),
    ._11(n2_bit_decoder_1__11));
  and and_1 (and_1_out, A___00, n2_bit_decoder_1__00);
  and and_2 (and_2_out, B___01, n2_bit_decoder_1__01);
  and and_3 (and_3_out, C___10, n2_bit_decoder_1__10);
  and and_4 (and_4_out, D___11, n2_bit_decoder_1__11);
  or or_1 (Selected_Output, and_1_out, and_2_out, and_3_out, and_4_out);
endmodule

module _4_Bit_4_Input_Multiplexer (
  input  [3:0] A___00,
  input  [3:0] B___01,
  input  [3:0] C___10,
  input  [3:0] D___11,
  input  in_5,
  input  in_6,
  output [3:0] Selected_Output
);

  wire [3:0] and_1_out, and_2_out, and_3_out, and_4_out;
  wire [3:3] n2_bit_decoder_1__00, n2_bit_decoder_1__01, n2_bit_decoder_1__10, n2_bit_decoder_1__11;

  _2_Bit_Decoder u_2_bit_decoder_1 (
    .A(in_5), .B(in_6), ._00(n2_bit_decoder_1__00[3]), ._01(n2_bit_decoder_1__01[3]),
    ._10(n2_bit_decoder_1__10[3]), ._11(n2_bit_decoder_1__11[3]));
  assign and_1_out = A___00 & {4{n2_bit_decoder_1__00[3]}};  // AND_Gate and_1, 4 bits wide
  assign and_2_out = B___01 & {4{n2_bit_decoder_1__01[3]}};  // AND_Gate and_2, 4 bits wide
  assign and_3_out = C___10 & {4{n2_bit_decoder_1__10[3]}};  // AND_Gate and_3, 4 bits wide
  assign and_4_out = D___11 & {4{n2_bit_decoder_1__11[3]}};  // AND_Gate and_4, 4 bits wide
  assign Selected_Output = and_1_out | and_2_out | and_3_out | and_4_out;  // OR_Gate or_1, 4 bits wide
endmodule
